# Fritzing sketch ResistanceNetworkUI (saved by Fritzing 0.9.4)
breadboards: 1

parts:
  part = Arduino Nano (Rev3.0)
  R2 = Resistor [tolerance=±5% resistance=4.7k package=THT]
  R1 = Resistor [tolerance=±5% resistance=820 package=THT]
  S1 = Pushbutton [package="[THT]"]
  S2 = Pushbutton [package="[THT]"]
  R4 = Resistor [tolerance=±5% resistance=10k package=THT]
  R3 = Resistor [tolerance=±5% resistance=6.8k package=THT]
  S4 = Pushbutton [package="[THT]"]
  S5 = Pushbutton [package="[THT]"]
  R5 = Resistor [tolerance=±5% resistance=56k package=THT]
  S6 = Pushbutton [package="[THT]"]
  R6 = Resistor [tolerance=±5% resistance=5.6k package=THT]
  R7 = Resistor [tolerance=±5% resistance=12k package=THT]
  S3 = Pushbutton [package="[THT]"]

nets:
  N1: part.GND, R6.Pin_1, R7.Pin_1
  N2: part.A5, S1.Pin_1, S1.Pin_2, S2.Pin_1, S2.Pin_2, S4.Pin_1, S4.Pin_2, S5.Pin_2, S6.Pin_3, S6.Pin_4, R7.Pin_0, S3.Pin_1, S3.Pin_2
  N3: part.AREF, R2.Pin_0, R1.Pin_0, R4.Pin_0, R3.Pin_0, R5.Pin_0
  N4: R2.Pin_1, S2.Pin_3, S2.Pin_4
  N5: R1.Pin_1, S1.Pin_3, S1.Pin_4
  N6: R4.Pin_1, S4.Pin_3, S4.Pin_4
  N7: R3.Pin_1, S3.Pin_4
  N8: S5.Pin_4, R5.Pin_1
  N9: S6.Pin_1, S6.Pin_2, R6.Pin_0
