# Fritzing sketch exampleardufocus (saved by Fritzing 0.9.9b)
circuit board: 8.46667cm x 5.64444cm

parts:
  Bauteil1 = Arduino Nano (Rev3.0)
  Pololu_A1 = Pololu A4988 [package=SO16]
  M1 = Stepper Motor - Bipolar
  S1 = Momentary Switch [package=ksa_sealed_tac_switch]
  S2 = Momentary Switch [package=ksa_sealed_tac_switch]
  S3 = Momentary Switch [package=ksa_sealed_tac_switch]
  Power_plug1 = Power plug
  C1 = Capacitor Polarized [package=panasonic_e]
  R1 = Temperature Sensor (Thermistor) [thermistor_type=NTC package=THT]
  R2 = Resistor [tolerance=±5% power=0.25 resistance=10k package=THT]
  C2 = Ceramic Capacitor [capacitance=100nF voltage=35V package="100 mil [THT, multilayer]"]
  LED1 = smd LED [color="Red (633nm)" package="0603 [SMD]"]
  LED2 = smd LED [color="Red (633nm)" package="0603 [SMD]"]
  LED3 = smd LED [color="Red (633nm)" package="0603 [SMD]"]

nets (from the breadboard view):
  N1: Bauteil1.RESET, C2.1
  GND: Bauteil1.GND, Pololu_A1.ENABLE, S1.4, S2.4, S3.4, Power_plug1.GND, C1.-, R1.pin_0, C2.0, LED1.cathode, LED2.cathode, LED3.cathode
  N2: Bauteil1.D2, LED3.anode
  N3: Bauteil1.D3, LED2.anode
  N4: Bauteil1.D4, LED1.anode
  N5: Bauteil1.D6, Pololu_A1.DIR
  N6: Bauteil1.D7, Pololu_A1.STEP
  N7: Bauteil1.D8, Pololu_A1.SLEEP
  N8: Bauteil1.D10, Pololu_A1.MS3
  N9: Bauteil1.D11/MOSI, Pololu_A1.MS2
  N10: Bauteil1.D12/MISO, Pololu_A1.MS1
  VIN: Bauteil1.VIN, Pololu_A1.VMOT, Power_plug1.VCC, C1.+
  5V: Bauteil1.5V, Pololu_A1.RESET, Pololu_A1.VDD, R2.Pin_1
  N11: Bauteil1.A4, S3.1
  N12: Bauteil1.A3, S2.1
  N13: Bauteil1.A2, S1.1
  N14: Bauteil1.A0, R1.pin_1, R2.Pin_0
  N15: Pololu_A1.1B, M1.D
  N16: Pololu_A1.1A, M1.B
  N17: Pololu_A1.2A, M1.C
  N18: Pololu_A1.2B, M1.A
